# Fritzing sketch esp8266_max98357a_audio_doorbell (saved by Fritzing 1.0.4)
breadboards: 1

parts:
  WeMos_D1_Mini1 = WeMos D1 Mini  # not connected
  Part1 = Adafruit MAX98357A I2S 3W Class D Amplifier [part_number="Adafruit #3006"]
  S1 = Pushbutton [package="[THT]"]
  SPKR1 = Loudspeaker  # not connected
  R1 = Resistor [tolerance=±5% power=0.25W resistance=4.7k package=THT]  # not connected

nets:
  N1: Part1.VIN, Part1.SD_MODE
  N2: Part1.GND, S1.Pin_3, S1.Pin_4
  N3: S1.Pin_1, S1.Pin_2

custom parts:
  Adafruit MAX98357A I2S 3W Class D Amplifier: Listen to this good news - we now have an all in one digital audio amp breakout board that works incredibly well with the Raspberry Pi! If you're looking for an easy and low cost way to get you digital sound files bumpin' then the MAX08357 I2S Amp Breakout is for you. It takes standard I2S digital audio input and, not only decodes it into analog, but also amplifies it directly into a speaker.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
